# Fritzing sketch SimuladorLecturaTarjetas.diagrama (saved by Fritzing 0.8.0b)
breadboards: 1

parts:
  Parte1 = Arduino Uno (Rev3)
  LED1 = smd LED [color="Red (633nm)" package="0805 [SMD]"]
  LED2 = smd LED [color="White (4500K)" package="0805 [SMD]"]
  LED3 = smd LED [color="Green (555nm)" package="0805 [SMD]"]
  S1 = Pushbutton [package="[SMD]"]

nets:
  N1: Parte1.GND, LED1.cathode, LED2.cathode, LED3.cathode, S1.Pin_1, S1.Pin_2
  N2: Parte1.D10_PWM/SS, LED1.anode
  N3: Parte1.D11_PWM/MOSI, LED3.anode
  N4: Parte1.D12/MISO, LED2.anode
  N5: Parte1.D2, S1.Pin_3, S1.Pin_4
